# Fritzing sketch schematic_fritzing (saved by Fritzing 1.0.6)
breadboards: 2

parts:
  HC-SR04_Sensor_1 = HC-SR04 Ultrasonic Distance Sensor
  R1 = Resistor [tolerance=±5% resistance=10k package="0603 [SMD]"]
  R2 = Resistor [tolerance=±5% power=0.25W resistance=10k package=THT]
  R3 = Resistor [tolerance=±5% resistance=10k package="0603 [SMD]"]
  M1 = DOIT Esp32 DevKit v1 (30 pins long, 11 pins width) [part_number=ESP32S-PIN30]
  OLED1 = OLED 128x64 I2C Monochrome Display GND-VDD
  S1 = Pushbutton [package="[THT]"]
  D1 = LTE-302 [package=lte-302]
  R4 = Resistor [tolerance=±5% resistance=220 package="1206 [SMD]"]
  Part1 = HC-SR501 Body Sensor Module
  U6 = 74HC595 [package="DIP16 [THT]"]
  7_Segment_4_Digit_Display2 = 7-SEGMENT-4DIGIT common cathode [part_number=HS420561K-32 package=7-segment-4digit-cathode]
  R5 = Resistor [tolerance=±5% resistance=1k package="2512 [SMD]"]
  R6 = Resistor [tolerance=±5% resistance=1k package="2512 [SMD]"]
  R7 = Resistor [tolerance=±5% resistance=1k package="2512 [SMD]"]
  R8 = Resistor [tolerance=±5% resistance=1k package="2512 [SMD]"]
  R9 = Resistor [tolerance=±5% resistance=1k package="2512 [SMD]"]
  R10 = Resistor [tolerance=±5% resistance=1k package="2512 [SMD]"]
  R11 = Resistor [tolerance=±5% resistance=1k package="2512 [SMD]"]

nets:
  N1: HC-SR04_Sensor_1.TRIG, R1.Pin_0
  N2: HC-SR04_Sensor_1.ECHO, M1.D25
  GND: HC-SR04_Sensor_1.GND, R3.Pin_1, M1.GND, OLED1.GND, S1.Pin_1, S1.Pin_2, D1.A, Part1.GND, U6.GND, U6.OE
  N3: R1.Pin_1, R2.Pin_1, M1.D26
  N4: R2.Pin_0, R3.Pin_0
  VCC: M1.3V3, Part1.VCC, U6.MR, U6.VCC
  N5: M1.D4, U6.DS
  N6: M1.RX2, 7_Segment_4_Digit_Display2.pin_6
  N7: M1.TX2, 7_Segment_4_Digit_Display2.pin_8
  N8: M1.D18, U6.SH_CP
  N9: M1.D19, U6.ST_CP
  N10: M1.D21, OLED1.SDA
  N11: M1.D22, OLED1.SCK
  N12: M1.D23, 7_Segment_4_Digit_Display2.pin_9
  N13: M1.D32, 7_Segment_4_Digit_Display2.pin_12
  N14: M1.D27, Part1.OUT
  N15: M1.D14, S1.Pin_3, S1.Pin_4
  N16: M1.D13, R4.Pin_1
  N17: D1.C, R4.Pin_0
  N18: U6.Q1, R7.Pin_1
  N19: U6.Q2, R10.Pin_0
  N20: U6.Q3, R9.Pin_0
  N21: U6.Q4, R8.Pin_0
  N22: U6.Q5, R5.Pin_1
  N23: U6.Q6, R11.Pin_0
  N24: U6.Q7, 7_Segment_4_Digit_Display2.pin_3
  N25: U6.Q0, R6.Pin_1
  N26: 7_Segment_4_Digit_Display2.pin_1, R8.Pin_1
  N27: 7_Segment_4_Digit_Display2.pin_2, R9.Pin_1
  N28: 7_Segment_4_Digit_Display2.pin_4, R10.Pin_1
  N29: 7_Segment_4_Digit_Display2.pin_5, R11.Pin_1
  N30: 7_Segment_4_Digit_Display2.pin_7, R7.Pin_0
  N31: 7_Segment_4_Digit_Display2.pin_10, R5.Pin_0
  N32: 7_Segment_4_Digit_Display2.pin_11, R6.Pin_0

custom parts:
  DOIT Esp32 DevKit v1 (30 pins long, 11 pins width): The DOIT Esp32 DevKit v1 is one of the development board created by DOIT to evaluate the ESP-WROOM-32 module. It is based on the ESP32 microcontroller that boasts Wifi, Bluetooth, Ethernet and Low Power support all in a single chip. (vanepp) made breadboard work, adjusted pin numbering and labels and reduced size of schematic and cleaned up pcb. This chip is 30pins long (2 x15) and 11 pins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
  OLED 128x64 I2C Monochrome Display GND-VDD: OLED 128x64 I2C Monochrome Display. Note: there are two variants of this part, this one is the GND VDD SCK SDA variant. The other is VDD GND SCK SDA. Make sure you select the part that matches your module as using the incorrect part will probably destroy your module! In addition the mounting holes are marked on silkscreen but not by default drilled. If you want drilled mounting holes, copy a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
  HC-SR501 Body Sensor Module: Pyroelectric Infrared PIR Motion Sensor Detector Module
  7-SEGMENT-4DIGIT common cathode: A 7 Segment 4 Digit common cathode display, with decimal points
